// Logisim project Yashika_ALU.circ as structural Verilog: 9 circuits, main circuit  Main ALU Circuit
module _16_Bit_AND (
  input  [15:0] A,
  input  [15:0] B,
  output [15:0] C
);

  assign C = A & B;  // AND_Gate and_1, 16 bits wide

  // Notes on the sheet:
  //   16-Bit AND
  //   A= 110 b= 60  C=44(All values are in binary)
endmodule

module _16_Bit_OR (
  input  [15:0] A,
  input  [15:0] B,
  output [15:0] C
);

  assign C = A | B;  // OR_Gate or_1, 16 bits wide

  // Notes on the sheet:
  //   16-Bit OR
endmodule

module _16_Bit_XOR (
  input  [15:0] A,
  input  [15:0] B,
  output [15:0] C
);

  assign C = A ^ B;  // XOR_Gate xor_1, 16 bits wide

  // Notes on the sheet:
  //   16-bit XOR
endmodule

module _16_Bit_Inverter (
  input  [15:0] A,
  output [15:0] C
);

  assign C = ~A;  // NOT_Gate not_1, 16 bits wide

  // Notes on the sheet:
  //   16-Bit Inverter
endmodule

module _16_Bit_Adder (
  input  Carry_in,
  input  [15:0] A,
  input  [15:0] B,
  input  Stand_for_S0_in_the_ALU,
  output Negative_flag,
  output [15:0] C,
  output Zero_flag,
  output Carry_flag,
  output Overflow_bit
);

  wire and_1_out, and_2_out, not_1_out, not_2_out, not_3_out, xor_1_out;

  Adder #(.width(16)) adder_1 (.a(A), .b(B), .out(C), .cin(Carry_in), .cout(Carry_flag));
  xor xor_1 (xor_1_out, B[15], Stand_for_S0_in_the_ALU);
  not not_1 (not_1_out, C[15]);
  not not_2 (not_2_out, xor_1_out);
  not not_3 (not_3_out, A[15]);
  Comparator #(.width(16)) comparator_1 (.a(C), .b({16{1'b0}}), .eq(Zero_flag));  // open: gt, lt
  and and_1 (and_1_out, xor_1_out, not_1_out, A[15]);
  and and_2 (and_2_out, not_2_out, not_3_out, C[15]);
  or or_1 (Overflow_bit, and_1_out, and_2_out);

  assign Negative_flag = C[15];

  // Notes on the sheet:
  //   16-Bit Adder
  //   Please notice that you need to generate the four flag bits for the adder.
endmodule

module _16_Bit_Subtractor (
  input  in_1,
  input  [15:0] A,
  input  [15:0] B,
  input  S0_ALU,
  output Negative_flag,
  output [15:0] C,
  output Zero_flag,
  output Borrow_flag,
  output out_9
);

  wire and_1_out, and_2_out, not_1_out, not_2_out, not_3_out, xor_1_out;

  Subtractor #(.width(16)) subtractor_1 (.a(A), .b(B), .out(C), .bin(in_1), .bout(Borrow_flag));
  xor xor_1 (xor_1_out, B[15], S0_ALU);
  not not_1 (not_1_out, Negative_flag);
  Comparator #(.width(16)) comparator_1 (.a(C), .b({16{1'b0}}), .eq(Zero_flag));  // open: gt, lt
  not not_2 (not_2_out, xor_1_out);
  not not_3 (not_3_out, A[15]);
  and and_1 (and_1_out, xor_1_out, not_1_out, A[15]);
  and and_2 (and_2_out, not_2_out, not_3_out, Negative_flag);
  or or_1 (out_9, and_1_out, and_2_out);

  // Notes on the sheet:
  //   16-Bit Subtractor
  //   Please notice that you need to generate the four flag bits for the subtractor
endmodule

module _16_Bit_Left_Shifter_Circuit (
  input  [15:0] A,
  input  [3:0] Data_shift,
  input  Enable,
  input  Clock_like,
  input  Clear_bit,
  output [15:0] C
);

  wire [3:0] B_q;

  Register #(.width(4)) B (.D(Data_shift), .en(Enable), .Q(B_q), .clk(Clock_like), .clr(Clear_bit));
  Shifter #(.width(16)) shifter_1 (.in(A), .\dist (B_q), .out(C));

  // Notes on the sheet:
  //   Shift A to left by B bits
  //   16-Bit Left Shifter Circuit
endmodule

module _16_Bit_Right_Shfit_Circuit (
  input  [15:0] A,
  input  [3:0] Data_shift,
  input  Enable,
  input  in_4,
  input  Clear_bit,
  output [15:0] C
);

  wire [3:0] register_1_q;

  Register #(.width(4)) register_1 (.D(Data_shift), .en(Enable), .Q(register_1_q), .clk(in_4), .clr(Clear_bit));
  Shifter #(.width(16), .shift("lr")) shifter_1 (.in(A), .\dist (register_1_q), .out(C));

  // Notes on the sheet:
  //   Shift A to Right by B bits
  //   16-Bit Right Shifter Circuit
endmodule

module Main_ALU_Circuit (
);


  // Notes on the sheet:
  //   Main ALU Circuit to Build
  //   Needs to use all the subcircuits you built
endmodule
